// Logisim project aluproj.circ as structural Verilog: 15 circuits, main circuit main
module main (
  input  [7:0] A,
  input  [7:0] B,
  input  in_3,
  input  [1:0] OPCODE,
  output [7:0] out_5
);

  wire clock_1_out, multiplexer_3_out;
  wire [7:0] bitwise_and_1_out_3, multiplexer_1_out, n8bitadder_1_out_4, register_1_q, register_2_q,
       right_logic_shift_1_output;

  Clock clock_1 (.out(clock_1_out));
  Register register_1 (.D(A), .Q(register_1_q), .clk(clock_1_out));  // open: en, clr
  Register register_2 (.D(B), .Q(register_2_q), .clk(clock_1_out));  // open: en, clr
  Bitwise_AND bitwise_and_1 (.A(register_1_q), .B(register_2_q), .out_3(bitwise_and_1_out_3));
  Multiplexer #(.width(8), .enable("false")) multiplexer_1 (
    .in0(register_1_q), .in1(register_2_q), .out(multiplexer_1_out), .sel(in_3));
  right_Logic_shift right_logic_shift_1 (.Input(multiplexer_1_out), .Output(right_logic_shift_1_output));
  _8bitadder u_8bitadder_1 (
    .ADD_SUB_CTRL(multiplexer_3_out), .A(register_1_q), .B(register_2_q), .out_4(n8bitadder_1_out_4));
  Multiplexer #(.select(2), .width(8), .enable("false")) multiplexer_2 (
    .in0(right_logic_shift_1_output), .in1(n8bitadder_1_out_4), .in2(n8bitadder_1_out_4),
    .in3(bitwise_and_1_out_3), .out(out_5), .sel(OPCODE));
  Multiplexer #(.select(2), .enable("false")) multiplexer_3 (
    .in0(1'b0), .in1(1'b0), .in2(1'b1), .in3(1'b0), .out(multiplexer_3_out), .sel(OPCODE));

  // Notes on the sheet:
  //   Bitshift Right 00
  //   Addition 01
  //   Subtraction 10
  //   Bitwise AND 11
endmodule

module Full_Adder (
  input  In,
  input  A,
  input  B,
  output Result,
  output Out
);

  wire and_1_out, and_2_out, xor_1_out;

  and and_1 (and_1_out, A, B, B);
  xor xor_1 (xor_1_out, A, B);
  or or_1 (Out, and_1_out, and_2_out);
  and and_2 (and_2_out, In, xor_1_out);
  xor xor_2 (Result, In, xor_1_out);
endmodule

module Adder_Sub (
  input  ADD_SUB_CTRL,
  input  [3:0] A,
  input  [3:0] B,
  output [3:0] Result,
  output Carry_OUT,
  output Overflow
);

  wire and_1_out, and_2_out, full_adder_1_out, full_adder_2_out, full_adder_3_out, not_1_out, not_2_out,
       not_3_out, xor_1_out, xor_2_out, xor_3_out, xor_4_out;

  xor xor_1 (xor_1_out, ADD_SUB_CTRL, B[0]);
  xor xor_2 (xor_2_out, ADD_SUB_CTRL, B[1]);
  xor xor_3 (xor_3_out, ADD_SUB_CTRL, B[2]);
  xor xor_4 (xor_4_out, ADD_SUB_CTRL, B[3]);
  not not_1 (not_1_out, xor_4_out);
  not not_2 (not_2_out, xor_4_out);
  Full_Adder full_adder_1 (.A(A[0]), .B(xor_1_out), .In(ADD_SUB_CTRL), .Out(full_adder_1_out), .Result(Result[0]));
  Full_Adder full_adder_2 (.A(A[1]), .B(xor_2_out), .In(full_adder_1_out), .Out(full_adder_2_out), .Result(Result[1]));
  Full_Adder full_adder_3 (.A(A[2]), .B(xor_3_out), .In(full_adder_2_out), .Out(full_adder_3_out), .Result(Result[2]));
  Full_Adder full_adder_4 (.A(A[3]), .B(xor_4_out), .In(full_adder_3_out), .Out(Carry_OUT), .Result(Result[3]));
  not not_3 (not_3_out, Result[3]);
  and and_1 (and_1_out, Result[3], not_2_out, not_1_out);
  and and_2 (and_2_out, not_3_out, A[3], xor_4_out);
  or or_1 (Overflow, and_1_out, and_2_out);
endmodule

module _8bitadder (
  input  ADD_SUB_CTRL,
  input  [7:0] A,
  input  [7:0] B,
  output [7:0] out_4
);

  Adder_Sub _4_Bit_Adder_SUB (
    .ADD_SUB_CTRL(ADD_SUB_CTRL), .A(A[7:4]), .B(B[3:0]), .Result(out_4[3:0]));  // open: Carry_OUT, Overflow
  Adder_Sub _4_Bit_Adder_SUB_2 (
    .ADD_SUB_CTRL(ADD_SUB_CTRL), .A(A[3:0]), .B(B[7:4]), .Result(out_4[7:4]));  // open: Carry_OUT, Overflow
endmodule

// B_AND
module Bitwise_AND (
  input  [7:0] A,
  input  [7:0] B,
  output [7:0] out_3
);

  and AND_1 (out_3[0], A[0], B[0]);
  and AND_2 (out_3[1], A[1], B[1]);
  and AND_3 (out_3[2], A[2], B[2]);
  and AND_4 (out_3[3], A[3], B[3]);
  and AND_5 (out_3[4], A[4], B[4]);
  and AND_6 (out_3[5], A[5], B[5]);
  and AND_7 (out_3[6], A[6], B[6]);
  and AND_8 (out_3[7], A[7], B[7]);
endmodule

// B_Right
module right_Logic_shift (
  input  [7:0] Input,
  output [7:0] Output
);


  assign Output = {Input[6:0], 1'b0};
  // also tied to GND on the sheet: Input[7]
endmodule

module BitWise_OR (
  input  [7:0] A,
  input  [7:0] B,
  output [7:0] out_3
);

  or or_1 (out_3[0], A[0], B[0]);
  or or_2 (out_3[1], A[1], B[1]);
  or or_3 (out_3[2], A[2], B[2]);
  or or_4 (out_3[3], A[3], B[3]);
  or or_5 (out_3[4], A[4], B[4]);
  or or_6 (out_3[5], A[5], B[5]);
  or or_7 (out_3[6], A[6], B[6]);
  or or_8 (out_3[7], A[7], B[7]);
endmodule

module Left_Logic_shift (
  input  [7:0] Input,
  output [7:0] Output
);


  assign Output = {1'b0, Input[7:1]};
endmodule

module BitWise_NOT (
  input  [7:0] Input,
  output [7:0] Output
);

  not not_1 (Output[0], Input[0]);
  not not_2 (Output[1], Input[1]);
  not not_3 (Output[2], Input[2]);
  not not_4 (Output[3], Input[3]);
  not not_5 (Output[4], Input[4]);
  not not_6 (Output[5], Input[5]);
  not not_7 (Output[6], Input[6]);
  not not_8 (Output[7], Input[7]);
endmodule

module ADDER (
  input  ADD_SUB_CTRL,
  input  [7:0] A,
  input  [7:0] B,
  output [7:0] out_4
);

  Adder_Sub _4_Bit_Adder_SUB (
    .ADD_SUB_CTRL(ADD_SUB_CTRL), .A(A[7:4]), .B(B[3:0]), .Result(out_4[3:0]));  // open: Carry_OUT, Overflow
  Adder_Sub _4_Bit_Adder_SUB_2 (
    .ADD_SUB_CTRL(ADD_SUB_CTRL), .A(A[3:0]), .B(B[7:4]), .Result(out_4[7:4]));  // open: Carry_OUT, Overflow
endmodule

module increment (
  input  [7:0] Input,
  output [7:0] out_2
);

  Adder adder_1 (.a(Input), .b({8{1'b1}}), .out(out_2));  // open: cin, cout
endmodule

module Decrement (
  input  [7:0] Input,
  output [7:0] out_2
);

  Subtractor subtractor_1 (.a(Input), .b({8{1'b1}}), .out(out_2));  // open: bin, bout
endmodule

module Comparison (
  input  [7:0] A,
  input  [7:0] B,
  output out_3,
  output out_4,
  output out_5
);

  Comparator comparator_1 (.a(A), .b(B), .gt(out_3), .eq(out_4), .lt(out_5));
endmodule

module scratch (
  input  in_1,
  input  [7:0] A,
  input  [7:0] B,
  input  in_4,
  input  in_5,
  input  in_6,
  input  [1:0] OPCODE,
  output [7:0] out_8
);

  wire clock_1_out;
  wire [7:0] bitwise_and_1_out_3, multiplexer_1_out, multiplexer_2_out, n8bitadder_1_out_4, register_1_q,
       register_2_q, right_logic_shift_1_output;

  Clock clock_1 (.out(clock_1_out));
  Register register_1 (.D(A), .Q(register_1_q), .clk(clock_1_out));  // open: en, clr
  Register register_2 (.D(B), .Q(register_2_q), .clk(clock_1_out));  // open: en, clr
  Bitwise_AND bitwise_and_1 (.A(register_1_q), .B(register_2_q), .out_3(bitwise_and_1_out_3));
  right_Logic_shift right_logic_shift_1 (.Input(multiplexer_1_out), .Output(right_logic_shift_1_output));
  Multiplexer #(.width(8), .enable("false")) multiplexer_1 (
    .in0(register_1_q), .in1(register_2_q), .out(multiplexer_1_out), .sel(in_4));
  _8bitadder u_8bitadder_1 (.ADD_SUB_CTRL(in_1), .A(register_1_q), .B(register_2_q), .out_4(n8bitadder_1_out_4));
  Multiplexer #(.width(8), .enable("false")) multiplexer_2 (
    .in0(n8bitadder_1_out_4), .in1(bitwise_and_1_out_3), .out(multiplexer_2_out), .sel(in_5));
  Multiplexer #(.select(2), .width(8), .enable("false")) multiplexer_3 (.sel(OPCODE));  // open: in0, in1, in2, in3, out
  Multiplexer #(.width(8), .enable("false")) multiplexer_4 (
    .in0(multiplexer_2_out), .in1(right_logic_shift_1_output), .out(out_8), .sel(in_6));

  // Notes on the sheet:
  //   Bitshift Right 00
  //   Addition 01
  //   Subtraction 10
  //   Bitwise AND 11
endmodule

module custom_mux (
  input  [7:0] in_1,
  input  [7:0] in_2,
  input  in_3,
  output [7:0] out_4
);

  wire [7:0] and_1_out, and_2_out, not_1_out;
  wire [7:1] undriven;

  assign not_1_out = ~{undriven, in_3};  // NOT_Gate not_1, 8 bits wide
  assign and_1_out = in_1 & not_1_out;  // AND_Gate and_1, 8 bits wide
  assign and_2_out = in_2 & {undriven, in_3};  // AND_Gate and_2, 8 bits wide
  assign out_4 = and_1_out | and_2_out;  // OR_Gate or_1, 8 bits wide
  // Pins of 1 and 8 bits meet at {undriven, in_3}
endmodule
